# Fritzing sketch Blink (saved by Fritzing 0.9.3b)
circuit board: 5.60165cm x 3.28261cm
breadboards: 1

parts:
  R1 = Resistor [tolerance=±5% resistance=220 package=THT]
  R2 = Resistor [tolerance=±5% resistance=220 package=THT]
  R3 = Resistor [tolerance=±5% resistance=220 package=THT]
  S1 = Pushbutton [package="[THT]"]
  S2 = Pushbutton [package="[THT]"]
  S3 = Pushbutton [package="[THT]"]
  L2 = LED - 5mm [color="Blue (470nm)" package="5 mm [THT]"]
  L3 = LED - 5mm [color="Green (555nm)" package="5 mm [THT]"]
  L1 = LED - 5mm [color="Red (633nm)" package="5 mm [THT]"]
  V1 = DC Power [voltage=3]
  Pad1 = Pad [width=12 height=9.03111111111111 connect=center]
  J6 = female pin header, 1 pin [form="♀ (female)"]
  J5 = female pin header, 1 pin [form="♀ (female)"]
  J4 = female pin header, 1 pin [form="♀ (female)"]
  J2 = female pin header, 1 pin [form="♀ (female)"]

nets:
  N1: R1.Pin_0, L1.anode
  N2: R1.Pin_1, R2.Pin_1, R3.Pin_1, V1.V+, J6.pin1, J5.pin1
  N3: R2.Pin_0, L2.anode
  N4: R3.Pin_0, L3.anode
  N5: S1.Pin_1, S1.Pin_2, S2.Pin_1, S2.Pin_2, S3.Pin_1, S3.Pin_2, V1.V-, Pad1.pad
  N6: S1.Pin_3, S1.Pin_4, L1.cathode
  N7: S2.Pin_3, S2.Pin_4, L2.cathode
  N8: S3.Pin_3, S3.Pin_4, L3.cathode
  N9: J4.pin1, J2.pin1

notes:
  Learn to Solder Kit
  Learn to Solder Kit 0.2
  learntosolderkit.com
  Blink
