# Fritzing sketch Hue (saved by Fritzing 0.9.3b)
circuit board: 3.28cm x 4.5cm
breadboards: 1

parts:
  V1 = DC Power [voltage=5]  # not connected
  Pad1 = Pad [width=12 height=9.03111111111111 connect=center]
  J2 = female pin header, 1 pin [form="♀ (female)"]  # not connected
  J4 = female pin header, 1 pin [form="♀ (female)"]  # not connected
  J5 = female pin header, 1 pin [form="♀ (female)"]
  J6 = female pin header, 1 pin [form="♀ (female)"]
  R = female pin header, 3 pins [form="♀ (female)"]
  S1 = Toggle Switch [package=THT]
  R1 = Resistor [tolerance=±5% resistance=220 package=THT]
  G = female pin header, 3 pins [form="♀ (female)"]
  R2 = Resistor [tolerance=±5% resistance=220 package=THT]
  B = female pin header, 3 pins [form="♀ (female)"]
  R3 = Resistor [tolerance=±5% resistance=220 package=THT]
  RGB_LED = female pin header, 4 pins [form="♀ (female)"]

nets (from the pcb view):
  N1: Pad1.pad, RGB_LED.pin3
  N2: J5.pin1, J6.pin1, S1.L1
  N3: R.pin2, S1.COM, G.pin2, B.pin2
  N4: R.pin3, R1.Pin_1
  N5: R1.Pin_0, RGB_LED.pin4
  N6: G.pin3, R2.Pin_1
  N7: R2.Pin_0, RGB_LED.pin2
  N8: B.pin3, R3.Pin_1
  N9: R3.Pin_0, RGB_LED.pin1

notes:
  Learn to Solder Kit 0.2
  -
  on | off
